# Fritzing sketch Etch-A-Sketch (saved by Fritzing 0.9.1b)

parts:
  Part1 = Arduino Pro Mini v13
  R1 = Trimmer Potentiometer [maximum_resistance=10kΩ package=THT]
  R2 = Trimmer Potentiometer [maximum_resistance=10kΩ package=THT]
  S1 = Pushbutton [package="[THT]"]
  S2 = Pushbutton [package="[THT]"]
  OLED1 = 128x64 Monochrom OLED Display with SPI Control

nets:
  N1: Part1.VCC, R1.leg2, R2.leg2
  N2: Part1.GND, R1.leg1, R2.leg1, S1.Pin_1, S2.Pin_1, S2.Pin_2
  N3: Part1.A1, R2.wiper
  N4: Part1.A0, R1.wiper
  N5: Part1.D13/SCK, OLED1.Clock
  N6: Part1.D11_PWM/MOSI, OLED1.Data
  N7: Part1.D10_PWM/SS, OLED1.CS
  N8: Part1.D9_PWM, OLED1.Reset
  N9: Part1.D8, OLED1.SA0/DC
  N10: Part1.D5_PWM, S1.Pin_3, S1.Pin_4
  N11: Part1.D4, S2.Pin_3, S2.Pin_4
